# Fritzing sketch SMLReader (saved by Fritzing 0.9.4)

parts:
  WeMos_D1_Mini1 = WeMos D1 Mini
  Q1 = LTR-301 [package=ltr-301]  # not connected
  R1 = Resistor [tolerance=±5% resistance=1k package="2010 [SMD]"]

nets:
  N1: WeMos_D1_Mini1.3V3, R1.Pin_1
  N2: WeMos_D1_Mini1.D2, R1.Pin_0

notes:
  1kΩ
  BPW 40
